# Fritzing sketch Project_4 (saved by Fritzing 0.9.3b)

parts:
  part = Raspberry Pi Pico
  X_Axis_Driver = L298 [package=multiwatt15]
  Y_Axis_Driver = L298 [package=multiwatt15]
  X_axis_Stepper = Stepper Motor - Bipolar
  Y_axis_Stepper = Stepper Motor - Bipolar
  Joystick = JOYSTICK_MINI [package=joystick_mini]
  Z_Up = SWITCH-MOMENTARY-2 [package=tactile_switch_tall]
  Z_Down = SWITCH-MOMENTARY-2 [package=tactile_switch_tall]
  S4 = SWITCH-MOMENTARY-2 [package=tactile_switch_tall]
  S5 = SWITCH-MOMENTARY-2 [package=tactile_switch_tall]
  S6 = SWITCH-MOMENTARY-2 [package=tactile_switch_tall]
  S7 = SWITCH-MOMENTARY-2 [package=tactile_switch_tall]
  V1 = DC Power [voltage=12V]
  Rotational_axis_Stepper = Basic Servo
  12v_to_5v_buck_converter = IC, DIP package, 4 pins

nets:
  N1: part.pin_4, Joystick.RIGHT
  N2: part.pin_5, Joystick.UP
  N3: part.pin_6, Joystick.LEFT
  N4: part.pin_7, Joystick.DOWN
  N5: part.pin_9, X_Axis_Driver.IN1
  N6: part.pin_10, X_Axis_Driver.IN2
  N7: part.pin_11, X_Axis_Driver.IN3
  N8: part.pin_12, X_Axis_Driver.IN4
  N9: part.pin_14, Y_Axis_Driver.IN1
  N10: part.pin_15, Y_Axis_Driver.IN2
  N11: part.pin_16, Y_Axis_Driver.IN3
  N12: part.pin_17, Y_Axis_Driver.IN4
  GND: part.pin_18, part.pin_23, part.pin_38, X_Axis_Driver.GND, Y_Axis_Driver.GND, Joystick.GND, Z_Up.2, Z_Down.2, S4.2, S5.2, S6.2, S7.2, V1.V-, Rotational_axis_Stepper.gnd, 12v_to_5v_buck_converter.pin2
  N13: part.pin_19, S4.1
  N14: part.pin_20, S7.1
  N15: part.pin_21, S6.1
  N16: part.pin_22, S5.1
  N17: part.pin_24, Rotational_axis_Stepper.pulse
  N18: part.pin_25, Z_Up.1
  N19: part.pin_26, Z_Down.1
  N20: part.pin_40, Rotational_axis_Stepper.vcc, 12v_to_5v_buck_converter.pin4
  N21: X_Axis_Driver.OUT1, X_axis_Stepper.A
  N22: X_Axis_Driver.OUT2, X_axis_Stepper.C
  N23: X_Axis_Driver.VS, Y_Axis_Driver.VS, V1.V+, 12v_to_5v_buck_converter.pin1
  N24: X_Axis_Driver.OUT3, X_axis_Stepper.B
  N25: X_Axis_Driver.OUT4, X_axis_Stepper.D
  N26: Y_Axis_Driver.OUT1, Y_axis_Stepper.A
  N27: Y_Axis_Driver.OUT2, Y_axis_Stepper.C
  N28: Y_Axis_Driver.OUT3, Y_axis_Stepper.B
  N29: Y_Axis_Driver.OUT4, Y_axis_Stepper.D

custom parts:
  Raspberry Pi Pico: Raspberry Pi Pico. Based around the RP2040 microcontroller the Pico is a low cost microcontroller device bringing Raspberry Pi quality, cost, and easy of use to the microcontroller space. Jan 2021, Split part in to two versions: tht (this one) and SMD. This one will drill holes for a .1 in header in pcb to allow plugging in the module as well as providing pads to solder the module to the top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
